# Fritzing sketch sousvide (saved by Fritzing 0.9.3b)
circuit board: 8.46667cm x 5.64444cm
breadboards: 1

parts:
  DS1 = DS18B20 1-Wire Temperature Sensor [part_number=DS18B20]
  WeMos_D1_Mini3 = WeMos D1 Mini
  Pump = Screw terminal - 2 pins [package=THT]
  SSR = Screw terminal - 2 pins [package=THT]
  Q1 = NPN-Transistor [package="TO92 [THT]"]
  Squix1 = OLED 0.96" 128x64 I2C SSD1306

nets:
  GND: DS1.GND, WeMos_D1_Mini3.G, Pump.pin2, SSR.pin2, Squix1.GND
  N1: DS1.DQ, WeMos_D1_Mini3.D0
  VDD: DS1.VDD, WeMos_D1_Mini3.3V3, Squix1.VCC
  N2: WeMos_D1_Mini3.5V, Q1.C
  N3: WeMos_D1_Mini3.D1, Squix1.SCL
  N4: WeMos_D1_Mini3.D2, Squix1.SCA
  N5: WeMos_D1_Mini3.D3, SSR.pin1
  N6: WeMos_D1_Mini3.D5, Q1.B
  N7: Pump.pin1, Q1.E

// code stored in the sketch: sousvide.ino
file:///C:/Users/emilbp/Downloads/ESP8266-12e-tht.fzpz
